# Fritzing sketch outdoor (saved by Fritzing 0.9.2b)
breadboards: 1

parts:
  JY-MCU = Arduino Nano (Rev3.0)
  Part1 = Bluetooth HC-05 Macho
  Part3 = Barometric Pressure Sensor - BMP085 Breakout  # not connected
  Part4 = Barometric Pressure Sensor - BMP085 Breakout

nets:
  GND: JY-MCU.GND, Part1.GND
  N1: JY-MCU.D11/MOSI, Part1.TXD
  N2: JY-MCU.D12/MISO, Part1.RXD
  5V: JY-MCU.5V, Part1.VCC
  3V3: JY-MCU.3V3, Part4.VCC
